// Logisim project control-logic.circ as structural Verilog: 1 circuit, main circuit control_logic
module control_logic (
  input  [31:0] inst,
  input  BrEq,
  input  BrLt,
  output PCSel,
  output RegWEn,
  output [2:0] ImmSel,
  output BrUn,
  output ASel,
  output BSel,
  output [3:0] ALUSel,
  output MemRW,
  output [1:0] WBSel,
  output CSRSel,
  output CSRWen
);

  wire and_25_out, and_26_out, and_27_out, and_28_out, and_29_out, and_30_out, auipc, beq, bge, bgeu, blt,
       bltu, bne, comparator_1_eq, comparator_2_eq, comparator_3_eq, comparator_4_eq, comparator_5_eq,
       comparator_6_eq, comparator_7_eq, comparator_8_eq, comparator_9_eq, comparator_10_eq,
       comparator_11_eq, comparator_12_eq, comparator_13_eq, comparator_14_eq, comparator_15_eq,
       comparator_16_eq, comparator_17_eq, comparator_18_eq, comparator_19_eq, comparator_20_eq,
       comparator_21_eq, comparator_22_eq, comparator_23_eq, comparator_24_eq, comparator_25_eq,
       comparator_26_eq, csrw, csrwi, enable_out_a, jal, jalr, lui, not_1_out, not_2_out, not_3_out,
       or_1_out, or_2_out, or_3_out, or_4_out, or_5_out, or_6_out;
  wire [2:0] priority_encoder_2_out;
  wire [4:0] priority_encoder_1_out;
  wire [5:0] bit_extender_2_out, input1, input_a, input_b;
  wire [16:0] and_1_out, and_2_out, and_3_out, and_4_out, and_5_out, and_6_out, and_7_out, and_8_out,
       and_9_out, and_10_out, and_11_out, and_12_out, and_13_out, and_14_out, and_15_out, and_16_out,
       and_17_out, and_18_out, and_19_out, and_20_out, and_21_out, and_22_out, and_23_out, and_24_out;

  ROM #(.addrWidth(6), .dataWidth(16)) rom_1 (
    .addr(input1), .data({RegWEn, ImmSel, BrUn, ASel, BSel, ALUSel, MemRW, WBSel, CSRSel, CSRWen}));
  assign and_1_out = {inst[31:25], inst[14:12], inst[6:0]} & 17'h3ff;  // AND_Gate and_1, 17 bits wide
  assign and_2_out = {inst[31:25], inst[14:12], inst[6:0]} & 17'h3ff;  // AND_Gate and_2, 17 bits wide
  assign and_3_out = {inst[31:25], inst[14:12], inst[6:0]} & 17'h3ff;  // AND_Gate and_3, 17 bits wide
  assign and_4_out = {inst[31:25], inst[14:12], inst[6:0]} & 17'h3ff;  // AND_Gate and_4, 17 bits wide
  assign and_5_out = {inst[31:25], inst[14:12], inst[6:0]} & 17'h3ff;  // AND_Gate and_5, 17 bits wide
  assign and_6_out = {inst[31:25], inst[14:12], inst[6:0]} & 17'h3ff;  // AND_Gate and_6, 17 bits wide
  assign and_7_out = {inst[31:25], inst[14:12], inst[6:0]} & 17'h3ff;  // AND_Gate and_7, 17 bits wide
  assign and_8_out = {inst[31:25], inst[14:12], inst[6:0]} & 17'h3ff;  // AND_Gate and_8, 17 bits wide
  assign and_9_out = {inst[31:25], inst[14:12], inst[6:0]} & 17'h3ff;  // AND_Gate and_9, 17 bits wide
  assign and_10_out = {inst[31:25], inst[14:12], inst[6:0]} & 17'h3ff;  // AND_Gate and_10, 17 bits wide
  assign and_11_out = {inst[31:25], inst[14:12], inst[6:0]} & 17'h3ff;  // AND_Gate and_11, 17 bits wide
  assign and_12_out = {inst[31:25], inst[14:12], inst[6:0]} & 17'h3ff;  // AND_Gate and_12, 17 bits wide
  assign and_13_out = {inst[31:25], inst[14:12], inst[6:0]} & 17'h3ff;  // AND_Gate and_13, 17 bits wide
  assign and_14_out = {inst[31:25], inst[14:12], inst[6:0]} & 17'h3ff;  // AND_Gate and_14, 17 bits wide
  assign and_15_out = {inst[31:25], inst[14:12], inst[6:0]} & 17'h3ff;  // AND_Gate and_15, 17 bits wide
  assign and_16_out = {inst[31:25], inst[14:12], inst[6:0]} & 17'h3ff;  // AND_Gate and_16, 17 bits wide
  assign and_17_out = {inst[31:25], inst[14:12], inst[6:0]} & 17'h3ff;  // AND_Gate and_17, 17 bits wide
  assign and_18_out = {inst[31:25], inst[14:12], inst[6:0]} & 17'h3ff;  // AND_Gate and_18, 17 bits wide
  assign and_19_out = {inst[31:25], inst[14:12], inst[6:0]} & 17'h7f;  // AND_Gate and_19, 17 bits wide
  assign and_20_out = {inst[31:25], inst[14:12], inst[6:0]} & 17'h7f;  // AND_Gate and_20, 17 bits wide
  assign and_21_out = {inst[31:25], inst[14:12], inst[6:0]} & 17'h7f;  // AND_Gate and_21, 17 bits wide
  assign and_22_out = {inst[31:25], inst[14:12], inst[6:0]} & 17'h3ff;  // AND_Gate and_22, 17 bits wide
  assign and_23_out = {inst[31:25], inst[14:12], inst[6:0]} & 17'h3ff;  // AND_Gate and_23, 17 bits wide
  assign and_24_out = {inst[31:25], inst[14:12], inst[6:0]} & 17'h3ff;  // AND_Gate and_24, 17 bits wide
  Comparator #(.width(17)) comparator_1 (
    .a({inst[31:25], inst[14:12], inst[6:0]}), .b(17'h33), .eq(comparator_1_eq));  // open: gt, lt
  Comparator #(.width(17)) comparator_2 (
    .a({inst[31:25], inst[14:12], inst[6:0]}), .b(17'h433), .eq(comparator_2_eq));  // open: gt, lt
  Comparator #(.width(17)) comparator_3 (
    .a({inst[31:25], inst[14:12], inst[6:0]}), .b(17'h8033), .eq(comparator_3_eq));  // open: gt, lt
  Comparator #(.width(17)) comparator_4 (
    .a({inst[31:25], inst[14:12], inst[6:0]}), .b(17'hb3), .eq(comparator_4_eq));  // open: gt, lt
  Comparator #(.width(17)) comparator_5 (
    .a({inst[31:25], inst[14:12], inst[6:0]}), .b(17'h4b3), .eq(comparator_5_eq));  // open: gt, lt
  Comparator #(.width(17)) comparator_6 (
    .a({inst[31:25], inst[14:12], inst[6:0]}), .b(17'h5b3), .eq(comparator_6_eq));  // open: gt, lt
  Comparator #(.width(17)) comparator_7 (
    .a({inst[31:25], inst[14:12], inst[6:0]}), .b(17'h133), .eq(comparator_7_eq));  // open: gt, lt
  Comparator #(.width(17)) comparator_8 (
    .a({inst[31:25], inst[14:12], inst[6:0]}), .b(17'h233), .eq(comparator_8_eq));  // open: gt, lt
  Comparator #(.width(17)) comparator_9 (
    .a({inst[31:25], inst[14:12], inst[6:0]}), .b(17'h2b3), .eq(comparator_9_eq));  // open: gt, lt
  Comparator #(.width(17)) comparator_10 (
    .a({inst[31:25], inst[14:12], inst[6:0]}), .b(17'h82b3), .eq(comparator_10_eq));  // open: gt, lt
  Comparator #(.width(17)) comparator_11 (
    .a({inst[31:25], inst[14:12], inst[6:0]}), .b(17'h333), .eq(comparator_11_eq));  // open: gt, lt
  Comparator #(.width(17)) comparator_12 (
    .a({inst[31:25], inst[14:12], inst[6:0]}), .b(17'h3b3), .eq(comparator_12_eq));  // open: gt, lt
  Comparator #(.width(17)) comparator_13 (.a(and_1_out), .b(17'h3), .eq(comparator_13_eq));  // open: gt, lt
  Comparator #(.width(17)) comparator_14 (.a(and_2_out), .b(17'h83), .eq(comparator_14_eq));  // open: gt, lt
  Comparator #(.width(17)) comparator_15 (.a(and_3_out), .b(17'h103), .eq(comparator_15_eq));  // open: gt, lt
  Comparator #(.width(17)) comparator_16 (.a(and_4_out), .b(17'h13), .eq(comparator_16_eq));  // open: gt, lt
  Comparator #(.width(17)) comparator_17 (.a(and_5_out), .b(17'h93), .eq(comparator_17_eq));  // open: gt, lt
  Comparator #(.width(17)) comparator_18 (.a(and_6_out), .b(17'h113), .eq(comparator_18_eq));  // open: gt, lt
  Comparator #(.width(17)) comparator_19 (.a(and_7_out), .b(17'h213), .eq(comparator_19_eq));  // open: gt, lt
  Comparator #(.width(17)) comparator_20 (
    .a({inst[31:25], inst[14:12], inst[6:0]}), .b(17'h293), .eq(comparator_20_eq));  // open: gt, lt
  Comparator #(.width(17)) comparator_21 (
    .a({inst[31:25], inst[14:12], inst[6:0]}), .b(17'h8293), .eq(comparator_21_eq));  // open: gt, lt
  Comparator #(.width(17)) comparator_22 (.a(and_8_out), .b(17'h313), .eq(comparator_22_eq));  // open: gt, lt
  Comparator #(.width(17)) comparator_23 (.a(and_9_out), .b(17'h393), .eq(comparator_23_eq));  // open: gt, lt
  Comparator #(.width(17)) comparator_24 (.a(and_10_out), .b(17'h23), .eq(comparator_24_eq));  // open: gt, lt
  Comparator #(.width(17)) comparator_25 (.a(and_11_out), .b(17'ha3), .eq(comparator_25_eq));  // open: gt, lt
  Comparator #(.width(17)) comparator_26 (.a(and_12_out), .b(17'h123), .eq(comparator_26_eq));  // open: gt, lt
  Comparator #(.width(17)) comparator_27 (.a(and_13_out), .b(17'h63), .eq(beq));  // open: gt, lt
  Comparator #(.width(17)) comparator_28 (.a(and_14_out), .b(17'he3), .eq(bne));  // open: gt, lt
  Comparator #(.width(17)) comparator_29 (.a(and_15_out), .b(17'h263), .eq(blt));  // open: gt, lt
  Comparator #(.width(17)) comparator_30 (.a(and_16_out), .b(17'h2e3), .eq(bge));  // open: gt, lt
  Comparator #(.width(17)) comparator_31 (.a(and_17_out), .b(17'h363), .eq(bltu));  // open: gt, lt
  Comparator #(.width(17)) comparator_32 (.a(and_18_out), .b(17'h3e3), .eq(bgeu));  // open: gt, lt
  Comparator #(.width(17)) comparator_33 (.a(and_19_out), .b(17'h17), .eq(auipc));  // open: gt, lt
  Comparator #(.width(17)) comparator_34 (.a(and_20_out), .b(17'h37), .eq(lui));  // open: gt, lt
  Comparator #(.width(17)) comparator_35 (.a(and_21_out), .b(17'h6f), .eq(jal));  // open: gt, lt
  Comparator #(.width(17)) comparator_36 (.a(and_22_out), .b(17'h67), .eq(jalr));  // open: gt, lt
  Comparator #(.width(17)) comparator_37 (.a(and_23_out), .b(17'hf3), .eq(csrw));  // open: gt, lt
  Comparator #(.width(17)) comparator_38 (.a(and_24_out), .b(17'h2f3), .eq(csrwi));  // open: gt, lt
  Priority_Encoder #(.select(5)) priority_encoder_1 (
    .in0(comparator_1_eq), .in1(comparator_2_eq), .in2(comparator_3_eq), .in3(comparator_4_eq),
    .in4(comparator_5_eq), .in5(comparator_6_eq), .in6(comparator_7_eq), .in7(comparator_8_eq),
    .in8(comparator_9_eq), .in9(comparator_10_eq), .in10(comparator_11_eq), .in11(comparator_12_eq),
    .in12(comparator_13_eq), .in13(comparator_14_eq), .in14(comparator_15_eq), .in15(comparator_16_eq),
    .in16(comparator_17_eq), .in17(comparator_18_eq), .in18(comparator_19_eq), .in19(comparator_20_eq),
    .in20(comparator_21_eq), .in21(comparator_22_eq), .in22(comparator_23_eq), .in23(comparator_24_eq),
    .in24(comparator_25_eq), .in25(comparator_26_eq), .in26(beq), .in27(bne), .in28(blt), .in29(bge),
    .in30(bltu), .in31(bgeu), .out(priority_encoder_1_out), .en_out(enable_out_a));  // open: gs, en_in
  Priority_Encoder priority_encoder_2 (
    .in0(auipc), .in1(lui), .in2(jal), .in3(jalr), .in4(csrw), .in5(csrwi), .out(priority_encoder_2_out),
    .en_in(enable_out_a));  // open: in6, in7, gs, en_out
  and and_25 (and_25_out, beq, BrEq);
  and and_26 (and_26_out, bne, not_1_out);
  not not_1 (not_1_out, BrEq);
  and and_27 (and_27_out, blt, BrLt);
  and and_28 (and_28_out, bge, not_2_out);
  not not_2 (not_2_out, BrLt);
  and and_29 (and_29_out, bltu, BrLt);
  and and_30 (and_30_out, bgeu, not_3_out);
  not not_3 (not_3_out, BrLt);
  or or_1 (or_1_out, jal, jalr);
  assign input_a = {{1{1'b0}}, priority_encoder_1_out};  // Bit_Extender bit_extender_1
  assign bit_extender_2_out = {{3{1'b0}}, priority_encoder_2_out};  // Bit_Extender bit_extender_2
  or or_2 (or_2_out, and_25_out, and_26_out);
  or or_3 (or_3_out, and_27_out, and_28_out);
  or or_4 (or_4_out, and_29_out, and_30_out);
  Adder #(.width(6)) adder_1 (.a(bit_extender_2_out), .b(6'b100000), .out(input_b));  // open: cin, cout
  or or_5 (or_5_out, or_2_out, or_3_out);
  or or_6 (or_6_out, or_5_out, or_4_out);
  Multiplexer #(.enable("false"), .width(6)) multiplexer_1 (
    .in0(input_a), .in1(input_b), .out(input1), .sel(enable_out_a));
  or or_7 (PCSel, or_6_out, or_1_out);

  // Other names for the same wires on the sheet: ctrl[16:0] = {inst[31:25], inst[14:12], inst[6:0]};
  //   op[6:0] = inst[6:0]; fun3[2:0] = inst[14:12]; fun7[6:0] = inst[31:25]

  // Notes on the sheet:
  //   INPUTS to your circuit
  //   contents of rom_1 (hex, n*v repeats v):
  //   8004 8104 8184 8024 8124 8164 8044 8084 80a4 81a4 80c4 80e4 9208 9208 9208 9204 9224 9244 9284 92a4
  //   93a4 92c4 92e4 2210 2210 2210 4*3600 3e00 3e00 d604 d3e4 c60c 920c 8001 e003
  //   ROM FOR CONTROL LOGIC
  //   DON'T CHANGE THE LOCATIONS OF THE INPUTS AND OUTPUTS!
  //   OUTPUT from your circuit
endmodule
