// Logisim project imm-gen.circ as structural Verilog: 1 circuit, main circuit imm_gen
module imm_gen (
  input  [31:0] inst,
  input  [2:0] ImmSel,
  output [31:0] imm
);

  wire [31:0] csmm0, imm0, sbmm0, smm0, ujmm0, umm0;

  Shifter #(.shift("ar"), .width(32)) shifter_1 (.in(inst), .\dist (5'b10100), .out(imm0));
  assign umm0 = inst & 32'hfffff000;  // AND_Gate and_1, 32 bits wide
  assign smm0 = {{20{inst[31]}}, {inst[31:25], inst[11:7]}};  // Bit_Extender bit_extender_1
  assign sbmm0 = {{19{inst[31]}}, {inst[31], inst[7], inst[30:25], inst[11:8], 1'b0}};  // Bit_Extender bit_extender_2
  assign ujmm0 = {{11{inst[31]}}, {inst[31], inst[19:12], inst[20], inst[30:21], 1'b0}};  // Bit_Extender bit_extender_3
  assign csmm0 = {{27{1'b0}}, inst[19:15]};  // Bit_Extender bit_extender_4
  Multiplexer #(.enable("false"), .select(3), .width(32)) multiplexer_1 (
    .in1(imm0), .in2(smm0), .in3(sbmm0), .in4(ujmm0), .in5(umm0), .in6(csmm0), .out(imm), .sel(ImmSel));  // open: in0, in7

  // Notes on the sheet:
  //   INPUTS to your circuit
  //   DON'T CHANGE THE LOCATIONS OF THE INPUTS AND OUTPUTS!
  //   OUTPUT from your circuit
endmodule
