// Logisim project regfile.circ as structural Verilog: 1 circuit, main circuit regfile
module regfile (
  input  [4:0] rs1,
  input  [4:0] rs2,
  input  [4:0] rd,
  input  [31:0] Write_Data,
  input  RegWEn,
  input  clk,
  output [31:0] ra,
  output [31:0] sp,
  output [31:0] t0,
  output [31:0] t1,
  output [31:0] t2,
  output [31:0] s0,
  output [31:0] s1,
  output [31:0] a0,
  output [31:0] Read_Data_1,
  output [31:0] Read_Data_2
);

  wire and_1_out, and_2_out, and_3_out, and_4_out, and_5_out, and_6_out, and_7_out, and_8_out, and_9_out,
       and_10_out, and_11_out, and_12_out, and_13_out, and_14_out, and_15_out, and_16_out, and_17_out,
       and_18_out, and_19_out, and_20_out, and_21_out, and_22_out, and_23_out, and_24_out, and_25_out,
       and_26_out, and_27_out, and_28_out, and_29_out, and_30_out, and_31_out, comparator_1_eq,
       comparator_2_eq, comparator_3_eq, comparator_4_eq, comparator_5_eq, comparator_6_eq, comparator_7_eq,
       comparator_8_eq, comparator_9_eq, comparator_10_eq, comparator_11_eq, comparator_12_eq,
       comparator_13_eq, comparator_14_eq, comparator_15_eq, comparator_16_eq, comparator_17_eq,
       comparator_18_eq, comparator_19_eq, comparator_20_eq, comparator_21_eq, comparator_22_eq,
       comparator_23_eq, comparator_24_eq, comparator_25_eq, comparator_26_eq, comparator_27_eq,
       comparator_28_eq, comparator_29_eq, comparator_30_eq, comparator_31_eq;
  wire [31:0] a0i, a1, a1i, a2, a2i, a3, a3i, a4, a4i, a5, a5i, a6, a6i, a7, a7i, gp, gpi, rai, s0i, s1i, s2,
       s2i, s3, s3i, s4, s4i, s5, s5i, s6, s6i, s7, s7i, s8, s8i, s9, s9i, s10, s10i, s11, s11i, spi, t0i,
       t1i, t2i, t3, t3i, t4, t4i, t5, t5i, t6, t6i, tp, tpi, x0, x0i;

  Register #(.width(32)) register_1 (.D({32{1'b0}}), .clk(clk), .Q(x0));  // open: en, clr
  Comparator #(.width(5)) comparator_1 (.a(rd), .b(5'b00001), .eq(comparator_1_eq));  // open: gt, lt
  Comparator #(.width(5)) comparator_2 (.a(rd), .b(5'b00010), .eq(comparator_2_eq));  // open: gt, lt
  Comparator #(.width(5)) comparator_3 (.a(rd), .b(5'b00101), .eq(comparator_3_eq));  // open: gt, lt
  Comparator #(.width(5)) comparator_4 (.a(rd), .b(5'b00110), .eq(comparator_4_eq));  // open: gt, lt
  Comparator #(.width(5)) comparator_5 (.a(rd), .b(5'b00111), .eq(comparator_5_eq));  // open: gt, lt
  Comparator #(.width(5)) comparator_6 (.a(rd), .b(5'b01000), .eq(comparator_6_eq));  // open: gt, lt
  Comparator #(.width(5)) comparator_7 (.a(rd), .b(5'b01001), .eq(comparator_7_eq));  // open: gt, lt
  Comparator #(.width(5)) comparator_8 (.a(rd), .b(5'b01010), .eq(comparator_8_eq));  // open: gt, lt
  Comparator #(.width(5)) comparator_9 (.a(rd), .b(5'b10100), .eq(comparator_9_eq));  // open: gt, lt
  Comparator #(.width(5)) comparator_10 (.a(rd), .b({5{1'b1}}), .eq(comparator_10_eq));  // open: gt, lt
  Comparator #(.width(5)) comparator_11 (.a(rd), .b(5'b10010), .eq(comparator_11_eq));  // open: gt, lt
  Comparator #(.width(5)) comparator_12 (.a(rd), .b(5'b10101), .eq(comparator_12_eq));  // open: gt, lt
  Comparator #(.width(5)) comparator_13 (.a(rd), .b(5'b10111), .eq(comparator_13_eq));  // open: gt, lt
  Comparator #(.width(5)) comparator_14 (.a(rd), .b(5'b11001), .eq(comparator_14_eq));  // open: gt, lt
  Comparator #(.width(5)) comparator_15 (.a(rd), .b(5'b11011), .eq(comparator_15_eq));  // open: gt, lt
  Comparator #(.width(5)) comparator_16 (.a(rd), .b(5'b11101), .eq(comparator_16_eq));  // open: gt, lt
  Register #(.width(32)) register_2 (.D(rai), .en(and_1_out), .clk(clk), .Q(ra));  // open: clr
  and and_1 (and_1_out, comparator_1_eq, RegWEn);
  Register #(.width(32)) register_3 (.D(spi), .en(and_2_out), .clk(clk), .Q(sp));  // open: clr
  and and_2 (and_2_out, comparator_2_eq, RegWEn);
  Register #(.width(32)) register_4 (.D(t0i), .en(and_3_out), .clk(clk), .Q(t0));  // open: clr
  and and_3 (and_3_out, comparator_3_eq, RegWEn);
  Register #(.width(32)) register_5 (.D(t1i), .en(and_4_out), .clk(clk), .Q(t1));  // open: clr
  and and_4 (and_4_out, comparator_4_eq, RegWEn);
  Register #(.width(32)) register_6 (.D(t2i), .en(and_5_out), .clk(clk), .Q(t2));  // open: clr
  and and_5 (and_5_out, comparator_5_eq, RegWEn);
  Register #(.width(32)) register_7 (.D(s0i), .en(and_6_out), .clk(clk), .Q(s0));  // open: clr
  and and_6 (and_6_out, comparator_6_eq, RegWEn);
  Register #(.width(32)) register_8 (.D(s1i), .en(and_7_out), .clk(clk), .Q(s1));  // open: clr
  and and_7 (and_7_out, comparator_7_eq, RegWEn);
  Register #(.width(32)) register_9 (.D(a0i), .en(and_8_out), .clk(clk), .Q(a0));  // open: clr
  and and_8 (and_8_out, comparator_8_eq, RegWEn);
  Register #(.width(32)) register_10 (.D(s4i), .en(and_9_out), .clk(clk), .Q(s4));  // open: clr
  and and_9 (and_9_out, comparator_9_eq, RegWEn);
  Register #(.width(32)) register_11 (.D(t6i), .en(and_10_out), .clk(clk), .Q(t6));  // open: clr
  and and_10 (and_10_out, comparator_10_eq, RegWEn);
  Register #(.width(32)) register_12 (.D(s2i), .en(and_11_out), .clk(clk), .Q(s2));  // open: clr
  and and_11 (and_11_out, comparator_11_eq, RegWEn);
  Register #(.width(32)) register_13 (.D(s5i), .en(and_12_out), .clk(clk), .Q(s5));  // open: clr
  and and_12 (and_12_out, comparator_12_eq, RegWEn);
  Register #(.width(32)) register_14 (.D(s7i), .en(and_13_out), .clk(clk), .Q(s7));  // open: clr
  and and_13 (and_13_out, comparator_13_eq, RegWEn);
  Register #(.width(32)) register_15 (.D(s9i), .en(and_14_out), .clk(clk), .Q(s9));  // open: clr
  and and_14 (and_14_out, comparator_14_eq, RegWEn);
  Register #(.width(32)) register_16 (.D(s11i), .en(and_15_out), .clk(clk), .Q(s11));  // open: clr
  and and_15 (and_15_out, comparator_15_eq, RegWEn);
  Register #(.width(32)) register_17 (.D(t4i), .en(and_16_out), .clk(clk), .Q(t4));  // open: clr
  and and_16 (and_16_out, comparator_16_eq, RegWEn);
  Demultiplexer #(.enable("false"), .select(5), .width(32)) demultiplexer_1 (
    .out0(x0i), .out1(rai), .out2(spi), .out3(gpi), .out4(tpi), .out5(t0i), .out6(t1i), .out7(t2i),
    .out8(s0i), .out9(s1i), .out10(a0i), .out11(a1i), .out12(a2i), .out13(a3i), .out14(a4i), .out15(a5i),
    .out16(a6i), .out17(a7i), .out18(s2i), .out19(s3i), .out20(s4i), .out21(s5i), .out22(s6i), .out23(s7i),
    .out24(s8i), .out25(s9i), .out26(s10i), .out27(s11i), .out28(t3i), .out29(t4i), .out30(t5i), .out31(t6i),
    .in(Write_Data), .sel(rd));
  Comparator #(.width(5)) comparator_17 (.a(rd), .b(5'b00011), .eq(comparator_17_eq));  // open: gt, lt
  Comparator #(.width(5)) comparator_18 (.a(rd), .b(5'b00100), .eq(comparator_18_eq));  // open: gt, lt
  Comparator #(.width(5)) comparator_19 (.a(rd), .b(5'b01011), .eq(comparator_19_eq));  // open: gt, lt
  Comparator #(.width(5)) comparator_20 (.a(rd), .b(5'b01100), .eq(comparator_20_eq));  // open: gt, lt
  Comparator #(.width(5)) comparator_21 (.a(rd), .b(5'b01101), .eq(comparator_21_eq));  // open: gt, lt
  Comparator #(.width(5)) comparator_22 (.a(rd), .b(5'b01110), .eq(comparator_22_eq));  // open: gt, lt
  Comparator #(.width(5)) comparator_23 (.a(rd), .b(5'b01111), .eq(comparator_23_eq));  // open: gt, lt
  Comparator #(.width(5)) comparator_24 (.a(rd), .b(5'b10000), .eq(comparator_24_eq));  // open: gt, lt
  Comparator #(.width(5)) comparator_25 (.a(rd), .b(5'b10001), .eq(comparator_25_eq));  // open: gt, lt
  Comparator #(.width(5)) comparator_26 (.a(rd), .b(5'b10011), .eq(comparator_26_eq));  // open: gt, lt
  Comparator #(.width(5)) comparator_27 (.a(rd), .b(5'b10110), .eq(comparator_27_eq));  // open: gt, lt
  Comparator #(.width(5)) comparator_28 (.a(rd), .b(5'b11000), .eq(comparator_28_eq));  // open: gt, lt
  Comparator #(.width(5)) comparator_29 (.a(rd), .b(5'b11010), .eq(comparator_29_eq));  // open: gt, lt
  Comparator #(.width(5)) comparator_30 (.a(rd), .b(5'b11100), .eq(comparator_30_eq));  // open: gt, lt
  Comparator #(.width(5)) comparator_31 (.a(rd), .b(5'b11110), .eq(comparator_31_eq));  // open: gt, lt
  Register #(.width(32)) register_18 (.D(gpi), .en(and_17_out), .clk(clk), .Q(gp));  // open: clr
  and and_17 (and_17_out, comparator_17_eq, RegWEn);
  Register #(.width(32)) register_19 (.D(tpi), .en(and_18_out), .clk(clk), .Q(tp));  // open: clr
  and and_18 (and_18_out, comparator_18_eq, RegWEn);
  Register #(.width(32)) register_20 (.D(a1i), .en(and_19_out), .clk(clk), .Q(a1));  // open: clr
  and and_19 (and_19_out, comparator_19_eq, RegWEn);
  Register #(.width(32)) register_21 (.D(a2i), .en(and_20_out), .clk(clk), .Q(a2));  // open: clr
  and and_20 (and_20_out, comparator_20_eq, RegWEn);
  Register #(.width(32)) register_22 (.D(a3i), .en(and_21_out), .clk(clk), .Q(a3));  // open: clr
  and and_21 (and_21_out, comparator_21_eq, RegWEn);
  Register #(.width(32)) register_23 (.D(a4i), .en(and_22_out), .clk(clk), .Q(a4));  // open: clr
  and and_22 (and_22_out, comparator_22_eq, RegWEn);
  Register #(.width(32)) register_24 (.D(a5i), .en(and_23_out), .clk(clk), .Q(a5));  // open: clr
  and and_23 (and_23_out, comparator_23_eq, RegWEn);
  Register #(.width(32)) register_25 (.D(a6i), .en(and_24_out), .clk(clk), .Q(a6));  // open: clr
  and and_24 (and_24_out, comparator_24_eq, RegWEn);
  Register #(.width(32)) register_26 (.D(a7i), .en(and_25_out), .clk(clk), .Q(a7));  // open: clr
  and and_25 (and_25_out, comparator_25_eq, RegWEn);
  Register #(.width(32)) register_27 (.D(s3i), .en(and_26_out), .clk(clk), .Q(s3));  // open: clr
  and and_26 (and_26_out, comparator_26_eq, RegWEn);
  Register #(.width(32)) register_28 (.D(s6i), .en(and_27_out), .clk(clk), .Q(s6));  // open: clr
  and and_27 (and_27_out, comparator_27_eq, RegWEn);
  Register #(.width(32)) register_29 (.D(s8i), .en(and_28_out), .clk(clk), .Q(s8));  // open: clr
  and and_28 (and_28_out, comparator_28_eq, RegWEn);
  Register #(.width(32)) register_30 (.D(s10i), .en(and_29_out), .clk(clk), .Q(s10));  // open: clr
  and and_29 (and_29_out, comparator_29_eq, RegWEn);
  Register #(.width(32)) register_31 (.D(t3i), .en(and_30_out), .clk(clk), .Q(t3));  // open: clr
  and and_30 (and_30_out, comparator_30_eq, RegWEn);
  Register #(.width(32)) register_32 (.D(t5i), .en(and_31_out), .clk(clk), .Q(t5));  // open: clr
  and and_31 (and_31_out, comparator_31_eq, RegWEn);
  Multiplexer #(.enable("false"), .select(5), .width(32)) multiplexer_1 (
    .in0(x0), .in1(ra), .in2(sp), .in3(gp), .in4(tp), .in5(t0), .in6(t1), .in7(t2), .in8(s0), .in9(s1),
    .in10(a0), .in11(a1), .in12(a2), .in13(a3), .in14(a4), .in15(a5), .in16(a6), .in17(a7), .in18(s2),
    .in19(s3), .in20(s4), .in21(s5), .in22(s6), .in23(s7), .in24(s8), .in25(s9), .in26(s10), .in27(s11),
    .in28(t3), .in29(t4), .in30(t5), .in31(t6), .out(Read_Data_1), .sel(rs1));
  Multiplexer #(.enable("false"), .select(5), .width(32)) multiplexer_2 (
    .in0(x0), .in1(ra), .in2(sp), .in3(gp), .in4(tp), .in5(t0), .in6(t1), .in7(t2), .in8(s0), .in9(s1),
    .in10(a0), .in11(a1), .in12(a2), .in13(a3), .in14(a4), .in15(a5), .in16(a6), .in17(a7), .in18(s2),
    .in19(s3), .in20(s4), .in21(s5), .in22(s6), .in23(s7), .in24(s8), .in25(s9), .in26(s10), .in27(s11),
    .in28(t3), .in29(t4), .in30(t5), .in31(t6), .out(Read_Data_2), .sel(rs2));

  // Other names for the same wires on the sheet: read_data1[31:0] = Read_Data_1; read_data2[31:0] = Read_Data_2;
  //   read_reg1[4:0] = rs1; read_reg2[4:0] = rs2; write_en = RegWEn; write_reg[4:0] = rd

  // Notes on the sheet:
  //   INPUTS to your circuit
  //   DON'T CHANGE THE LOCATIONS OF THE INPUTS AND OUTPUTS!
  //   These are DEBUG/TEST outputs from your circuit.
  //   OUTPUTS from your circuit
endmodule
